// Digital circuit signal generator and character indexer.dig as structural Verilog
module signal_generator_and_character_indexer (
  input  pxl
);

  wire _7404_3_pin8, _7404_3_pin10, _7404_3_pin12, _7408_1_pin4, _7408_1_pin5, _7408_1_pin6, _7408_1_pin8,
       _7408_1_pin9, _7408_1_pin10, _7408_1_pin11, _7408_2_pin3, _7408_2_pin6, _7408_2_pin8, _7420_1_pin1,
       _7420_1_pin5, _7420_1_pin6, _7458_1_pin1, _7458_1_pin3, _7458_1_pin4, _7458_1_pin5, _7458_1_pin8,
       _7458_1_pin12, _7458_1_pin13, _7458_2_pin6, _7458_2_pin8, _74161_1_pin1, _74161_1_pin15,
       _74161_2_pin15, _74161_3_pin13, _74161_4_pin15, _74161_5_pin15, _744075_1_pin3, _744075_1_pin4,
       _744075_1_pin6, _744075_1_pin8, _744075_1_pin9, _744075_1_pin10, _744075_1_pin13, _744075_2_pin9,
       not_1_out;
  wire [7:0] img_d;
  wire [15:0] _7420_1_pin2;

  _74161 _74161_1 (
    .pin1(_74161_1_pin1), .pin2(pxl), .pin3(1'b0), .pin4(1'b0), .pin5(1'b0), .pin6(1'b0), .pin7(1'b1),
    .pin8(1'b0), .pin9(1'b1), .pin10(1'b1), .pin11(_7420_1_pin2[2]), .pin12(_7420_1_pin2[1]),
    .pin13(_7420_1_pin2[0]), .pin15(_74161_1_pin15), .pin16(1'b1));  // open: pin14
  _74161 _74161_2 (
    .pin1(_74161_1_pin1), .pin2(pxl), .pin3(1'b0), .pin4(1'b0), .pin5(1'b0), .pin6(1'b0),
    .pin7(_74161_1_pin15), .pin8(1'b0), .pin9(1'b1), .pin10(1'b1), .pin11(_7420_1_pin2[6]),
    .pin12(_7420_1_pin2[5]), .pin13(_7420_1_pin2[4]), .pin14(_7420_1_pin2[3]), .pin15(_74161_2_pin15),
    .pin16(1'b1));
  _74161 _74161_3 (
    .pin1(_74161_1_pin1), .pin2(pxl), .pin3(1'b0), .pin4(1'b0), .pin5(1'b0), .pin6(1'b0),
    .pin7(_74161_1_pin15), .pin8(1'b0), .pin9(1'b1), .pin10(_74161_2_pin15), .pin13(_74161_3_pin13),
    .pin14(_7420_1_pin2[7]), .pin16(1'b1));  // open: pin11, pin12, pin15
  _7420 _7420_1 (
    .pin1(_7420_1_pin1), .pin2(_7420_1_pin2[10]), .pin4(_7420_1_pin2[9]), .pin5(_7420_1_pin5),
    .pin6(_7420_1_pin6), .pin7(1'b0), .pin8(_74161_1_pin1), .pin9(_7420_1_pin2[4]), .pin10(_7420_1_pin2[7]),
    .pin12(_74161_3_pin13), .pin13(1'b1), .pin14(1'b1));  // open: pin3, pin11
  _74161 _74161_4 (
    .pin1(_7420_1_pin6), .pin2(_74161_1_pin1), .pin3(1'b0), .pin4(1'b0), .pin5(1'b0), .pin6(1'b0),
    .pin7(1'b1), .pin8(1'b0), .pin9(1'b1), .pin10(1'b1), .pin11(_7420_1_pin2[10]), .pin12(_7420_1_pin2[9]),
    .pin13(_7420_1_pin2[8]), .pin14(_7420_1_pin5), .pin15(_74161_4_pin15), .pin16(1'b1));
  _74161 _74161_5 (
    .pin1(_7420_1_pin6), .pin2(_74161_1_pin1), .pin3(1'b0), .pin4(1'b0), .pin5(1'b0), .pin6(1'b0),
    .pin7(_74161_4_pin15), .pin8(1'b0), .pin9(1'b1), .pin10(1'b1), .pin11(_7420_1_pin2[14]),
    .pin12(_7420_1_pin2[13]), .pin13(_7420_1_pin2[12]), .pin14(_7420_1_pin2[11]), .pin15(_74161_5_pin15),
    .pin16(1'b1));
  _74161 _74161_6 (
    .pin1(_7420_1_pin6), .pin2(_74161_1_pin1), .pin3(1'b0), .pin4(1'b0), .pin5(1'b0), .pin6(1'b0),
    .pin7(_74161_4_pin15), .pin8(1'b0), .pin9(1'b1), .pin10(_74161_5_pin15), .pin13(_7420_1_pin1),
    .pin14(_7420_1_pin2[15]), .pin16(1'b1));  // open: pin11, pin12, pin15
  not not_1 (not_1_out, _7420_1_pin1);
  _7408 _7408_1 (
    .pin1(1'b0), .pin2(1'b0), .pin4(_7408_1_pin4), .pin5(_7408_1_pin5), .pin6(_7408_1_pin6), .pin7(1'b0),
    .pin8(_7408_1_pin8), .pin9(_7408_1_pin9), .pin10(_7408_1_pin10), .pin11(_7408_1_pin11),
    .pin12(_7408_1_pin8), .pin13(_7408_1_pin6), .pin14(1'b1));  // open: pin3
  _7404 _7404_1 (
    .pin1(1'b0), .pin3(1'b0), .pin5(1'b0), .pin7(1'b0), .pin8(_7408_1_pin10), .pin9(_74161_3_pin13),
    .pin10(_7408_1_pin9), .pin11(_7420_1_pin1), .pin13(_7408_1_pin11), .pin14(1'b1));  // open: pin2, pin4, pin6, pin12
  _7458 _7458_1 (
    .pin1(_7458_1_pin1), .pin2(1'b1), .pin3(_7458_1_pin3), .pin4(_7458_1_pin4), .pin5(_7458_1_pin5),
    .pin6(_7408_1_pin5), .pin7(1'b0), .pin8(_7458_1_pin8), .pin9(_7420_1_pin2[5]), .pin10(_7420_1_pin2[4]),
    .pin11(_7420_1_pin2[3]), .pin12(_7458_1_pin12), .pin13(_7458_1_pin13), .pin14(1'b1));
  _7404 _7404_2 (
    .pin1(_7420_1_pin2[6]), .pin2(_7458_1_pin5), .pin3(_7420_1_pin2[7]), .pin4(_7458_1_pin4),
    .pin5(_74161_3_pin13), .pin6(_7458_1_pin3), .pin7(1'b0), .pin8(_7458_1_pin13), .pin9(_7420_1_pin2[3]),
    .pin10(_7458_1_pin12), .pin11(_7420_1_pin2[4]), .pin12(_7458_1_pin1), .pin13(_7420_1_pin2[5]),
    .pin14(1'b1));
  _744075 _744075_1 (
    .pin1(_7420_1_pin2[9]), .pin2(_7420_1_pin2[11]), .pin3(_744075_1_pin3), .pin4(_744075_1_pin4),
    .pin5(1'b0), .pin6(_744075_1_pin6), .pin7(1'b0), .pin8(_744075_1_pin8), .pin9(_744075_1_pin9),
    .pin10(_744075_1_pin10), .pin11(_744075_1_pin9), .pin12(_744075_1_pin6), .pin13(_744075_1_pin13),
    .pin14(1'b1));
  _7404 _7404_3 (
    .pin1(_7420_1_pin2[8]), .pin2(_744075_1_pin8), .pin3(_7420_1_pin2[10]), .pin4(_744075_1_pin4),
    .pin5(_7420_1_pin2[12]), .pin6(_744075_1_pin3), .pin7(1'b0), .pin8(_7404_3_pin8),
    .pin9(_7420_1_pin2[13]), .pin10(_7404_3_pin10), .pin11(_7420_1_pin2[14]), .pin12(_7404_3_pin12),
    .pin13(_7420_1_pin2[15]), .pin14(1'b1));
  _7458 _7458_2 (
    .pin1(not_1_out), .pin2(not_1_out), .pin3(_744075_1_pin3), .pin4(not_1_out), .pin5(_7404_3_pin8),
    .pin6(_7458_2_pin6), .pin7(1'b0), .pin8(_7458_2_pin8), .pin9(1'b1), .pin10(_7404_3_pin12),
    .pin11(not_1_out), .pin12(1'b1), .pin13(_7404_3_pin10), .pin14(1'b1));
  _744075 _744075_2 (
    .pin1(_7458_1_pin8), .pin2(_7458_1_pin5), .pin3(_7404_3_pin8), .pin4(_7404_3_pin10),
    .pin5(_7404_3_pin12), .pin6(_744075_1_pin13), .pin7(1'b0), .pin8(_7458_1_pin3), .pin9(_744075_2_pin9),
    .pin10(_7408_1_pin4), .pin11(1'b0), .pin12(_7458_2_pin8), .pin13(_7458_2_pin6), .pin14(1'b1));
  ROM #(.AddrBits(16), .Bits(8)) img (.A(_7420_1_pin2), .sel(_7408_1_pin11), .D(img_d));
  VGA vga_1 (.R(_7408_2_pin8), .G(_7408_2_pin3), .B(_7408_2_pin6), .H(_744075_2_pin9), .V(_744075_1_pin10), .C(pxl));
  _7408 _7408_2 (
    .pin1(img_d[3]), .pin2(_7408_1_pin11), .pin3(_7408_2_pin3), .pin4(img_d[6]), .pin5(_7408_1_pin11),
    .pin6(_7408_2_pin6), .pin7(1'b0), .pin8(_7408_2_pin8), .pin9(img_d[0]), .pin10(_7408_1_pin11),
    .pin12(1'b1), .pin13(1'b1), .pin14(1'b1));  // open: pin11

  // Notes on the sheet:
  //   pxl: Hz: 2147483647
  //   Pixel clock divider
  //   Pixel horizontal
  //   Column counter
  //   Line counter
  //   Pixel vertical
  //   !C
  //   !B
  //   !A
  //   !D
  //   !E
  //   !F
  //   High during hvis
  //   Low during hsync
  //   High during vvis
  //   Low during vsync
  //   contents of img (hex, n*v repeats v):
  //   256*ff,8*e0,8*1c,8*e0,8*1c,8*e0,8*1c,8*e0,8*1c,8*e0,8*1c,8*e0
  //   ,8*1c,8*e0,8*1c,8*e0,8*1c,8*e0,8*1c,8*e0,8*1c,8*e0,8*1c,8*e0,8*1c
  //   ,8*e0,8*1c,8*e0,8*1c,8*e0,8*1c,8*e0,8*1c,8*ff,8*0,232*ff
endmodule
